# Fritzing sketch Schematic (saved by Fritzing 0.9.3b)
breadboards: 1

parts:
  Raspberry_Pi_1 = Raspberry Pi 3 [part_number=RPI-3-V1.2]
  Cmod_A1 = Cmod A7
  R2 = Resistor [tolerance=±5% resistance=220 package=THT]
  S1 = Pushbutton [package=THT]
  R3 = Resistor [tolerance=±5% resistance=220 package=THT]
  LED1 = LED - 5mm [color="Red (633nm)" package="5 mm [THT]"]

nets:
  N1: Raspberry_Pi_1.GPIO10, Cmod_A1.2
  N2: Raspberry_Pi_1.GPIO9, Cmod_A1.1
  N3: Raspberry_Pi_1.GPIO11, Cmod_A1.3
  N4: Raspberry_Pi_1.GPIO25, Cmod_A1.4
  N5: Raspberry_Pi_1.GND, Cmod_A1.G
  N6: R2.Pin_0, S1.leg0
  N7: S1.leg1, R3.Pin_0
  N8: R3.Pin_1, LED1.anode

custom parts:
  Cmod A7: The Digilent Cmod A7 is a small, 48-pin DIP form factor board built around a Xilinx Artix 7 FPGA. The board also includes a USB-JTAG programming circuit, USB-UART bridge, clock source, Pmod host connector, SRAM, Quad SPI Flash, and basic I/O devices. These components make it a formidable, albeit compact, platform for digital logic circuits and Microblaze embedded softcore processor designs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
